# Fritzing sketch massroutepy (saved by Fritzing 0.8.0b)
perfboards: 2

parts:
  LED2 = LED - 5mm [color="Red (633nm)" package="5 mm [THT]"]
  LED3 = LED - 5mm [color="Green (555nm)" package="5 mm [THT]"]
  LED4 = LED - 5mm [color="Red (633nm)" package="5 mm [THT]"]
  LED5 = LED - 5mm [color="Green (555nm)" package="5 mm [THT]"]
  LED6 = LED - 5mm [color="Red (633nm)" package="5 mm [THT]"]
  Raspberry_Pi1 = Raspberry Pi
  LED7 = LED - 5mm [color="Green (555nm)" package="5 mm [THT]"]
  U3 = 74HC595 SMD [package="SO16 [SMD]"]
  U4 = 74HC595 SMD [package="SO16 [SMD]"]
  LED8 = LED - 5mm [color="Red (633nm)" package="5 mm [THT]"]
  LED9 = LED - 5mm [color="Green (555nm)" package="5 mm [THT]"]
  LED10 = LED - 5mm [color="Red (633nm)" package="5 mm [THT]"]
  LED11 = LED - 5mm [color="Green (555nm)" package="5 mm [THT]"]
  LED12 = LED - 5mm [color="Green (555nm)" package="5 mm [THT]"]
  LED13 = LED - 5mm [color="Red (633nm)" package="5 mm [THT]"]
  C1 = Ceramic Capacitor [capacitance=0.1µF voltage=50V package="100 mil [THT, multilayer]"]  # not connected
  C2 = Ceramic Capacitor [capacitance=0.1µF voltage=50V package="100 mil [THT, multilayer]"]  # not connected

nets:
  N1: LED2.anode, U3.Q1
  N2: LED3.anode, U3.Q0
  N3: LED4.anode, U3.Q3
  N4: LED5.anode, U3.Q2
  N5: LED6.cathode, LED7.cathode, U3.GND
  N6: LED6.anode, U3.Q5
  N7: Raspberry_Pi1.GPIO0, U3.DS
  N8: LED7.anode, U3.Q4
  N9: U3.Q7', U4.DS
  N10: U4.Q1, LED13.anode
  N11: U4.Q2, LED9.anode
  N12: U4.Q3, LED8.anode
  N13: U4.Q4, LED12.anode
  N14: U4.Q5, LED10.anode
  N15: U4.GND, U4.OE, LED12.cathode
  N16: U4.Q0, LED11.anode
